# Fritzing sketch Bubbler Electronics (saved by Fritzing 0.9.1b)
circuit board: 8.46667cm x 5.64444cm
breadboards: 1

parts:
  Part1 = Arduino Uno (Rev3)
  M1 = DC Motor
  R1 = Resistor [tolerance=±5% resistance=1k package=THT]
  D1 = Rectifier Diode [part_number=1N4001 package="300 mil [THT]"]
  PowerLED = LED - 5mm [color="Green (570nm)" package="5 mm [THT]"]
  Monitor_LED = LED - 5mm [color="Yellow (595nm)" package="5 mm [THT]"]
  Pressurising_LED = LED - 5mm [color="Orange (620nm)" package="5 mm [THT]"]
  R2 = Resistor [tolerance=±5% resistance=2.2k package=THT]
  R3 = Resistor [tolerance=±5% resistance=2.2k package=THT]
  R4 = Resistor [tolerance=±5% resistance=2.2k package=THT]
  R5 = Resistor [tolerance=±0.1% resistance=1k package=THT]
  R6 = Resistor [tolerance=±5% resistance=1M package=THT]
  Q1 = TRANSISTOR_NPN [package=to-92]
  Q1_2 = TRANSISTOR_NPN [part_number=2N2222 package=to-92]
  HSCDANN005PGSA1 = Honeywell HSC series pressure sensors [chip_label="HSC (SPI)" package="DIP (Dual Inline) [THT]"]
  Part2 = DeadOn RTC - DS3234 Breakout

nets:
  N1: Part1.D11_PWM/MOSI, Part2.MOSI
  N2: Part1.D12/MISO, HSCDANN005PGSA1.MISO, Part2.MISO
  N3: Part1.D13/SCK, HSCDANN005PGSA1.SCLK, Part2.SCLK
  N4: Part1.D3_PWM, R1.Pin_0
  N5: Part1.D4, Pressurising_LED.anode
  N6: Part1.D5_PWM, Monitor_LED.anode
  N7: Part1.D6_PWM, PowerLED.anode
  N8: Part1.D7, R5.Pin_1
  5V: Part1.5V, M1.pin_1, D1.cathode, R2.Pin_0, R3.Pin_0, R4.Pin_0, HSCDANN005PGSA1.+5, Part2.VCC
  GND: Part1.GND, R6.Pin_0, Q1.E, Q1_2.E, HSCDANN005PGSA1.GND, Part2.GND
  N9: M1.pin_2, D1.anode, Q1.C, Q1_2.C
  N10: R1.Pin_1, Q1.B, Q1_2.B
  N11: PowerLED.cathode, R3.Pin_1
  N12: Monitor_LED.cathode, R4.Pin_1
  N13: Pressurising_LED.cathode, R2.Pin_1
  N14: R5.Pin_0, R6.Pin_1, HSCDANN005PGSA1.SS

custom parts:
  Honeywell HSC series pressure sensors: A high accuracy air pressure sensor. Reports dry air pressures with 0.25% accuracy, includes temperature compensation. 5V part, SPI digital interface, 5PSI gauge pressure.

// code stored in the sketch: Bubbler.ino
#include <SPI.h>
#include "pins.h"
#include <SSC.h>
#include <Wire.h>
#include <SPI.h>
#include <DS3234.h>

SSC pressure_sensor(0x00, PRESSURE);
int MIN_RAW = 1638;
int MAX_RAW = 14746;
int BUFF_MAX = 80;
int ERROR = (MAX_RAW - MIN_RAW) / 400; // 0.25%

void print_datestamp() {
	char buff[BUFF_MAX];
	struct ts t;
	DS3234_init(CLOCK, DS3234_INTCN);
	DS3234_get(CLOCK, &t);

	// Current time
	snprintf(buff, BUFF_MAX, "%d/%02d/%02dT%02d:%02d:%02d", t.year, t.mon, t.mday, t.hour, t.min, t.sec);
	Serial.print(buff);
	}

void printReading() {
	print_datestamp();
	Serial.print(", ");
	Serial.print(pressure_sensor.pressure());
	Serial.print(", ");
	Serial.println(pressure_sensor.temperature());
	}

/*
How a reading is taken:

1. Start off with a pressure reading.

2. Blow some air into the tube.

3. If the pressure in the tube doesn't change significantly (i.e.: by more than the margin of error of the sensor), consider the tube evacuated, and the air pressure to be at equilibrium with the water pressure.

4. If the pressure does change, go back to step 1.

There is some finessing required in order to ensure that each "blow" is likely to change the overall pressure.
*/
void getPressureReading() {
	boolean charging = 1;
	boolean highpressure = 0;
	int old_pressure; // pressures are raw readings ("counts") from HSC sensor
	int new_pressure;

	pressure_sensor.start();
	pressure_sensor.update();
	new_pressure = pressure_sensor.pressure_Raw();

	while (charging) {
		old_pressure = new_pressure;
		highpressure = (new_pressure > (0.9 * MAX_RAW));
		if (highpressure) {
			charging = 0;
			Serial.println("HIGH PRESSURE!");
			digitalWrite(WARNLED, HIGH);
			break;
			}
		else {
			digitalWrite(WARNLED, LOW);
			}
		if (charging) {
			digitalWrite(MOTOR, HIGH);
			int pump_duration = 50;
			delay(pump_duration);
			digitalWrite(MOTOR, LOW);
			delay(500); // allow for pump motor inertia, and escape of some bubbles
			}
		pressure_sensor.update();
		new_pressure = pressure_sensor.pressure_Raw();
		charging = (abs(new_pressure - old_pressure) > ERROR);
		}
	pressure_sensor.stop();
	printReading();
	}

void setup() {
	// put your setup code here, to run once:
	setup_pins();
	DS3234_init(CLOCK, DS3234_INTCN || DS3234_EOSC);
	Serial.begin(115200);
	pressure_sensor.setMinRaw(1638);
	pressure_sensor.setMaxRaw(14746);
	pressure_sensor.setMinPressure(0.0);
	pressure_sensor.setMaxPressure(351.5); // cm H20, instead of PSI
	pressure_sensor.setTemperatureCompensated(1);
	Serial.print("Initialising pressure sensor: ");
	Serial.println(pressure_sensor.start());
	Serial.print("Maximum pressure is ");
	Serial.println(pressure_sensor.maxPressure());
	Serial.println("UTC, pressure (cmH20), temperature (C)");
	pressure_sensor.start();
	pressure_sensor.update();
	pressure_sensor.stop();
}

void loop() {
	// put your main code here, to run repeatedly:
	getPressureReading();
	delay(60000);
}
